# Fritzing sketch A2 sketch (saved by Fritzing 0.9.3b)
breadboards: 1

parts:
  R1 = Resistor [tolerance=±5% resistance=220 package=THT]
  Q1 = PNP-Transistor [package="TO92 [THT]"]
  J1 = Piezo Speaker
  Raspberry_Pi_1 = Raspberry Pi 3 [part_number=RPI-3-V1.2]

nets:
  N1: R1.Pin_0, Raspberry_Pi_1.GPIO17
  N2: R1.Pin_1, Q1.E
  N3: Q1.B, J1.pin1
  N4: Q1.C, Raspberry_Pi_1.GPIO7
  N5: J1.pin2, Raspberry_Pi_1.5V
